# Fritzing sketch GENAS Hardware Diagram straight (saved by Fritzing 0.9.3b)
circuit board: 8.67914cm x 5.78103cm
breadboards: 2

parts:
  Raspberry_Pi_1 = Raspberry Pi 3 [part_number=RPI-3-V1.2]
  LED1 = LED - 5mm [color="Red (633nm)" package="5 mm [THT]"]
  LED2 = LED - 5mm [color="Green (560nm)" package="5 mm [THT]"]
  LED3 = LED - 5mm [color="Yellow (595nm)" package="5 mm [THT]"]
  DS1 = DS18B20 1-Wire Temperature Sensor [part_number=DS18B20]
  R1 = Resistor [tolerance=±5% resistance=4.7k package=THT]
  Part1 = Adafruit TCS34725 RGB Color Sensor [part_number="Adafruit #1334"]
  Blue_light_emitter = LED - 5mm [color="Blue (470nm)" package="5 mm [THT]"]
  R2 = Resistor [tolerance=±5% resistance=220 package=THT]
  MIC1 = Microphone  # not connected
  SP1 = SPEAKER [package=pcb_mount_speaker]  # not connected
  U1 = LCD-16X2 [package=lcd-16x2]
  R3 = Trimmer Potentiometer [maximum_resistance=10kΩ package=THT]
  Part2 = Adafruit TSL2561 [part_number="Adafruit #439"]
  R4 = Resistor [tolerance=±5% resistance=330 package="2010 [SMD]"]
  Blue_light_emitter1 = LED - 5mm [color="Blue (470nm)" package="5 mm [THT]"]
  Blue_light_emitter2 = LED - 5mm [color="Blue (470nm)" package="5 mm [THT]"]
  Blue_light_emitter3 = LED - 5mm [color="Blue (470nm)" package="5 mm [THT]"]
  Blue_light_emitter4 = LED - 5mm [color="Blue (470nm)" package="5 mm [THT]"]
  Blue_light_emitter5 = LED - 5mm [color="Blue (470nm)" package="5 mm [THT]"]
  Blue_light_emitter6 = LED - 5mm [color="Blue (470nm)" package="5 mm [THT]"]
  S1 = Pushbutton [package="[SMD]"]
  R5 = Resistor [tolerance=±5% resistance=1k package=THT]  # not connected
  LED4 = LED - 5mm [color="White (6500K)" package="5 mm [THT]"]
  LED5 = LED - 5mm [color="Blue (470nm)" package="5 mm [THT]"]

nets (from the breadboard view):
  3V3: Raspberry_Pi_1.3v3, Raspberry_Pi_1.3V3, Part1.VIN, Part2.VIN
  N1: Raspberry_Pi_1.GPIO2, Part1.SDA, Part2.SDA
  N2: Raspberry_Pi_1.GPIO3, Part1.SCL, Part2.SCL
  N3: Raspberry_Pi_1.GPIO4, DS1.DQ, R1.Pin_0
  GND: Raspberry_Pi_1.GND, DS1.GND, Part1.GND, R2.Pin_1, U1.VSS, U1.R_W, U1.K, R3.leg1, Part2.GND, R4.Pin_0
  N4: Raspberry_Pi_1.GPIO5, LED5.anode
  N5: Raspberry_Pi_1.GPIO6, LED4.anode
  N6: Raspberry_Pi_1.GPIO19, LED2.anode
  N7: Raspberry_Pi_1.GPIO26, Blue_light_emitter.anode, Blue_light_emitter1.anode, Blue_light_emitter2.anode, Blue_light_emitter3.anode, Blue_light_emitter4.anode, Blue_light_emitter5.anode, Blue_light_emitter6.anode
  N8: Raspberry_Pi_1.GPIO21, S1.Pin_1, S1.Pin_2
  N9: Raspberry_Pi_1.GPIO20, LED1.anode
  N10: Raspberry_Pi_1.GPIO16, LED3.anode
  N11: Raspberry_Pi_1.GPIO7, U1.RS
  N12: Raspberry_Pi_1.GPIO8, U1.E
  N13: Raspberry_Pi_1.GPIO25, U1.DB4
  N14: Raspberry_Pi_1.GPIO24, U1.DB5
  N15: Raspberry_Pi_1.GPIO23, U1.DB6
  N16: Raspberry_Pi_1.GPIO18, U1.DB7
  VDD: Raspberry_Pi_1.5V, DS1.VDD, R1.Pin_1, U1.VDD, U1.A, R3.leg2, S1.Pin_3, S1.Pin_4
  N17: LED1.cathode, LED2.cathode, LED3.cathode, R4.Pin_1, LED4.cathode, LED5.cathode
  N18: Blue_light_emitter.cathode, R2.Pin_0, Blue_light_emitter1.cathode, Blue_light_emitter2.cathode, Blue_light_emitter3.cathode, Blue_light_emitter4.cathode, Blue_light_emitter5.cathode, Blue_light_emitter6.cathode
  N19: U1.VO, R3.wiper

custom parts:
  Adafruit TCS34725 RGB Color Sensor: Your electronics can now see in dazzling color with this lovely color light sensor. We found the best color sensor on the market, the TCS34725, which has RGB and Clear light sensing elements. An IR blocking filter, integrated on-chip and localized to the color sensing photodiodes, minimizes the IR spectral component of the incoming light and allows color measurements to be made accurately. The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
  Adafruit TSL2561: The TSL2561 luminosity sensor is an advanced digital light sensor, ideal for use in a wide range of light situations. Compared to low cost CdS cells, this sensor is more precise, allowing for exact lux calculations and can be configured for different gain/timing ranges to detect light ranges from up to 0.1 - 40,000+ Lux on the fly. The best part of this sensor is that it contains both infrared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
