# Fritzing sketch GENAS Hardware Diagram (saved by Fritzing 0.9.3b)
circuit board: 8.67914cm x 5.78103cm
breadboards: 1

parts:
  Raspberry_Pi_1 = Raspberry Pi 3 [part_number=RPI-3-V1.2]
  LED1 = LED - 5mm [color="Red (633nm)" package="5 mm [THT]"]  # not connected
  LED2 = LED - 5mm [color="Green (560nm)" package="5 mm [THT]"]  # not connected
  LED3 = LED - 5mm [color="Yellow (595nm)" package="5 mm [THT]"]  # not connected
  DS1 = DS18B20 1-Wire Temperature Sensor [part_number=DS18B20]
  R1 = Resistor [tolerance=±5% resistance=4.7k package=THT]
  Part1 = Adafruit TCS34725 RGB Color Sensor [part_number="Adafruit #1334"]
  Blue_light_emitter = LED - 5mm [color="Blue (470nm)" package="5 mm [THT]"]
  R2 = Resistor [tolerance=±5% resistance=220 package=THT]
  MIC1 = Microphone  # not connected
  SP1 = SPEAKER [package=pcb_mount_speaker]  # not connected
  U1 = LCD-16X2 [package=lcd-16x2]  # not connected

nets:
  3V3: Raspberry_Pi_1.3v3, Raspberry_Pi_1.3V3, DS1.VDD, R1.Pin_1, Part1.VIN
  N1: Raspberry_Pi_1.GPIO2, Part1.SDA
  N2: Raspberry_Pi_1.GPIO3, Part1.SCL
  N3: Raspberry_Pi_1.GPIO4, DS1.DQ, R1.Pin_0
  N4: Raspberry_Pi_1.GPIO26, Blue_light_emitter.cathode
  GND: Raspberry_Pi_1.GND, DS1.GND, Part1.GND, R2.Pin_1
  N5: Blue_light_emitter.anode, R2.Pin_0

custom parts:
  Adafruit TCS34725 RGB Color Sensor: Your electronics can now see in dazzling color with this lovely color light sensor. We found the best color sensor on the market, the TCS34725, which has RGB and Clear light sensing elements. An IR blocking filter, integrated on-chip and localized to the color sensing photodiodes, minimizes the IR spectral component of the incoming light and allows color measurements to be made accurately. The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
